# Fritzing sketch Wiring_fritzing (saved by Fritzing 0.9.4)

parts:
  Q1 = Basic FET P-Channel [part_number=IRF4905 package="TO220 [THT]"]
  Buck_DC/DC = RioRand LM2596
  L1_2_2mH = Inductor [package="400 mil [THT]"]
  iRobot_Create_2_Brush_Motor = screw terminal, 2 pins
  R2 = Resistor [tolerance=±5% resistance=1k package=THT]
  iRobot_Create_2_Serial_Plug = screw terminal, 2 pins
  Power_Output_to_Raspberry_Pi = screw terminal, 2 pins
  C1 = Ceramic Capacitor [capacitance=47nF voltage=35V package="100 mil [THT, multilayer]"]
  C2 = Electrolytic Capacitor [capacitance=330µF voltage=35V package="100 mil [THT, electrolytic]"]
  D2 = Schottky Diode [part_number=1N5817 package="300 mil [THT]"]
  D1 = Schottky Diode [part_number=1N5822 package="300 mil [THT]"]
  LED2 = LED - 5mm [color="Red (633nm)" package="5 mm [THT]"]
  R3 = Resistor [tolerance=±5% resistance=1.1k package=THT]
  LED3 = LED - 5mm [color="Green (555nm)" package="5 mm [THT]"]
  R4 = Resistor [tolerance=±5% resistance=1.1k package=THT]

nets:
  N1: Q1.gate, R2.Pin_1
  N2: Q1.drain, C2.+, D1.anode
  N3: Q1.source, iRobot_Create_2_Serial_Plug.pin2, R3.Pin_1
  N4: Buck_DC/DC.Pin_1, C1.1, D2.cathode, D1.cathode
  N5: Buck_DC/DC.Pin_2, iRobot_Create_2_Brush_Motor.pin1, iRobot_Create_2_Serial_Plug.pin1, C1.0, C2.-, LED2.cathode, LED3.cathode
  N6: Buck_DC/DC.Pin_3, Power_Output_to_Raspberry_Pi.pin1
  N7: Buck_DC/DC.Pin_4, Power_Output_to_Raspberry_Pi.pin2
  N8: L1_2_2mH.pin_0, iRobot_Create_2_Brush_Motor.pin2
  N9: L1_2_2mH.pin_1, R2.Pin_0, D2.anode, R4.Pin_1
  N10: LED2.anode, R3.Pin_0
  N11: LED3.anode, R4.Pin_0
